// Logisim project leonardofalango.circ as structural Verilog: 12 circuits, main circuit processador
module processador (
  input  [15:0] in_1,
  input  in_2,
  input  in_3
);

  wire clock_1_out, enable, isMov, isOp, not_1_out, not_2_out, not_3_out, not_4_out, not_5_out, not_6_out,
       not_7_out, or_2_out, or_3_out;
  wire [3:0] a, b, op, opTrans;
  wire [15:0] data, ulaout;

  or or_1 (enable, isOp, isMov);
  // Probe on a
  Clock clock_1 (.out(clock_1_out));
  // Probe on b
  reg_ula reg_ula_1 (
    .in_5(enable), .in_7(in_2), .in_8(opTrans), .in_1(a), .in_3(b), .in_4(clock_1_out), .in_6(in_3),
    .ULAOUT(ulaout));  // open: data
  // Probe on opTrans
  // Probe on data
  // Probe on opTrans
  Multiplexer #(.select(4), .width(4)) multiplexer_1 (
    .in8(4'b0111), .in9(4'b1010), .in10(4'b0001), .in11(4'b0100), .in12(4'b1101), .in13(4'b0110),
    .in14(4'b0000), .in15(4'b0011), .out(opTrans), .sel(op));  // open: in0, in1, in2, in3, in4, in5, in6, in7, en
  not not_1 (not_1_out, in_1[12]);
  and and_1 (isOp, not_1_out, not_2_out, not_3_out, not_4_out);
  not not_2 (not_2_out, in_1[13]);
  not not_3 (not_3_out, in_1[14]);
  not not_4 (not_4_out, in_1[15]);
  and and_2 (isMov, in_1[12], not_5_out, not_6_out, not_7_out);
  not not_5 (not_5_out, in_1[13]);
  not not_6 (not_6_out, in_1[14]);
  not not_7 (not_7_out, in_1[15]);
  Multiplexer #(.width(16)) multiplexer_2 (
    .in0(ulaout), .in1({{8{1'b0}}, in_1[7:0]}), .out(data), .sel(isMov));  // open: en
  Multiplexer #(.width(4)) multiplexer_3 (.in1(in_1[11:8]), .out(op), .sel(isOp));  // open: in0, en
  Multiplexer #(.width(4)) multiplexer_4 (.in0(in_1[11:8]), .in1(in_1[7:4]), .out(a), .sel(or_2_out));  // open: en
  or or_2 (or_2_out, isOp, 1'b0);
  Multiplexer #(.width(4)) multiplexer_5 (.in1(in_1[3:0]), .out(b), .sel(or_3_out));  // open: in0, en
  or or_3 (or_3_out, isOp, 1'b0);

  // Other names for the same wires on the sheet: addressA[3:0] = in_1[11:8]; input[15:0] = in_1; s2[3:0] = in_1[11:8];
  //   c[7:0] = in_1[7:0]; s3[3:0] = in_1[7:4]; s4[3:0] = in_1[3:0]; start[3:0] = in_1[15:12]
endmodule

// 1
module reg_ula (
  input  [3:0] in_1,
  input  [15:0] data,
  input  [3:0] in_3,
  input  in_4,
  input  in_5,
  input  in_6,
  input  in_7,
  input  [3:0] in_8,
  output [15:0] ULAOUT
);

  wire [11:0] crr, next;
  wire [15:0] reg_1_saidaa, reg_1_saidab;

  Register #(.width(12)) register_1 (.D(next), .en(1'b1), .Q(crr), .clk(in_4), .clr(in_6));
  Adder #(.width(12)) adder_1 (.a(crr), .b(12'h1), .out(next));  // open: cin, cout
  // Probe on reg_1_saidaa
  // Probe on reg_1_saidaa
  // Probe on ULAOUT
  Reg reg_1 (
    .Clock(in_4), .Enable(in_5), .Reset(in_7), .AddressA(in_1), .AddressB(in_3), .Data(data),
    .SaidaA(reg_1_saidaa), .SaidaB(reg_1_saidab));
  ULA ula_1 (.a(reg_1_saidaa), .b(reg_1_saidab), .Result(ULAOUT), .Operation(in_8));  // open: isEqual
  // Probe on reg_1_saidab
  // Probe on reg_1_saidab

  // Other names for the same wires on the sheet: clk = in_4; rst = in_6
endmodule

module HalfSum (
  input  a,
  input  b,
  output Sum,
  output CarryOut
);

  xor xor_1 (Sum, a, b);
  and and_1 (CarryOut, a, b);
endmodule

module FullSum (
  input  a,
  input  b,
  input  CarryIn,
  output Sum,
  output CarryOut
);

  wire halfsum_1_carryout, halfsum_1_sum, halfsum_2_carryout;

  HalfSum halfsum_1 (.a(a), .b(b), .Sum(halfsum_1_sum), .CarryOut(halfsum_1_carryout));
  HalfSum halfsum_2 (.a(halfsum_1_sum), .b(CarryIn), .Sum(Sum), .CarryOut(halfsum_2_carryout));
  or or_1 (CarryOut, halfsum_2_carryout, halfsum_1_carryout);
endmodule

module Sum (
  input  in_1,
  input  [15:0] in_2,
  input  [15:0] in_3,
  output [15:0] out_4,
  output CarryOut
);

  wire fullsum_1_carryout, fullsum_2_carryout, fullsum_3_carryout, fullsum_4_carryout, fullsum_5_carryout,
       fullsum_6_carryout, fullsum_7_carryout, fullsum_8_carryout, fullsum_9_carryout, fullsum_10_carryout,
       fullsum_11_carryout, fullsum_12_carryout, fullsum_13_carryout, fullsum_14_carryout,
       fullsum_15_carryout;

  FullSum fullsum_1 (.a(in_3[0]), .b(in_2[0]), .CarryIn(in_1), .Sum(out_4[0]), .CarryOut(fullsum_1_carryout));
  FullSum fullsum_2 (
    .a(in_3[1]), .b(in_2[1]), .CarryIn(fullsum_1_carryout), .Sum(out_4[1]), .CarryOut(fullsum_2_carryout));
  FullSum fullsum_3 (
    .a(in_3[2]), .b(in_2[2]), .CarryIn(fullsum_2_carryout), .Sum(out_4[2]), .CarryOut(fullsum_3_carryout));
  FullSum fullsum_4 (
    .a(in_3[3]), .b(in_2[3]), .CarryIn(fullsum_3_carryout), .Sum(out_4[3]), .CarryOut(fullsum_4_carryout));
  FullSum fullsum_5 (
    .a(in_3[4]), .b(in_2[4]), .CarryIn(fullsum_4_carryout), .Sum(out_4[4]), .CarryOut(fullsum_5_carryout));
  FullSum fullsum_6 (
    .a(in_3[5]), .b(in_2[5]), .CarryIn(fullsum_5_carryout), .Sum(out_4[5]), .CarryOut(fullsum_6_carryout));
  FullSum fullsum_7 (
    .a(in_3[6]), .b(in_2[6]), .CarryIn(fullsum_6_carryout), .Sum(out_4[6]), .CarryOut(fullsum_7_carryout));
  FullSum fullsum_8 (
    .a(in_3[7]), .b(in_2[7]), .CarryIn(fullsum_7_carryout), .Sum(out_4[7]), .CarryOut(fullsum_8_carryout));
  FullSum fullsum_9 (
    .a(in_3[8]), .b(in_2[8]), .CarryIn(fullsum_8_carryout), .Sum(out_4[8]), .CarryOut(fullsum_9_carryout));
  FullSum fullsum_10 (
    .a(in_3[9]), .b(in_2[9]), .CarryIn(fullsum_9_carryout), .Sum(out_4[9]), .CarryOut(fullsum_10_carryout));
  FullSum fullsum_11 (
    .a(in_3[10]), .b(in_2[10]), .CarryIn(fullsum_10_carryout), .Sum(out_4[10]), .CarryOut(fullsum_11_carryout));
  FullSum fullsum_12 (
    .a(in_3[11]), .b(in_2[11]), .CarryIn(fullsum_11_carryout), .Sum(out_4[11]), .CarryOut(fullsum_12_carryout));
  FullSum fullsum_13 (
    .a(in_3[12]), .b(in_2[12]), .CarryIn(fullsum_12_carryout), .Sum(out_4[12]), .CarryOut(fullsum_13_carryout));
  FullSum fullsum_14 (
    .a(in_3[13]), .b(in_2[13]), .CarryIn(fullsum_13_carryout), .Sum(out_4[13]), .CarryOut(fullsum_14_carryout));
  FullSum fullsum_15 (
    .a(in_3[14]), .b(in_2[14]), .CarryIn(fullsum_14_carryout), .Sum(out_4[14]), .CarryOut(fullsum_15_carryout));
  FullSum fullsum_16 (.a(in_3[15]), .b(in_2[15]), .CarryIn(fullsum_15_carryout), .Sum(out_4[15]), .CarryOut(CarryOut));

  // Other names for the same wires on the sheet: lucas = in_2[11]; joao = in_2[12]; roberto = in_2[13];
  //   leonardo = in_2[14]; carioca = in_2[15]; matheus = in_3[11]; jorge = in_3[12]; felipe = in_3[13];
  //   santos = in_3[14]; robson = in_3[15]
endmodule

module If (
  input  in_1,
  input  in_2,
  input  in_3
);

  wire and_1_out, and_2_out, not_1_out;

  not not_1 (not_1_out, in_2);
  and and_1 (and_1_out, in_1, not_1_out);
  and and_2 (and_2_out, in_2, in_3);
  // OR_Gate or_1 has open pins: in0=and_1_out, in1=and_2_out, out=open
endmodule

module ULA (
  input  [15:0] a,
  input  [15:0] b,
  input  [3:0] Operation,
  output [15:0] Result,
  output isEqual
);

  wire outGreater, outLess;
  wire [15:0] outAnd, outDec, outDiv, outInc, outLeftShift, outMult, outNand, outOr, outRightShift, outShift,
       outSub, outSum, outXor, undriven;

  Multiplexer #(.select(4), .width(16)) multiplexer_1 (
    .in0(outInc), .in1(outMult), .in2(outDec), .in4(outDiv), .in5({{15{1'b0}}, outLess}),
    .in6(outRightShift), .in7(outSum), .in8(undriven), .in9(outNand), .in10(outSub),
    .in11({{15{1'b0}}, outGreater}), .in12(outXor), .in13(outShift), .in14(outOr), .in15(outAnd),
    .out(Result), .sel(Operation));  // open: in3, en
  Subtractor #(.width(16)) subtractor_1 (.a(a), .b(16'h1), .out(outDec));  // open: bin, bout
  Adder #(.width(16)) adder_1 (.a(a), .b(16'h1), .out(outInc));  // open: cin, cout
  Adder #(.width(16)) adder_2 (.a(a), .b(b), .out(outSum));  // open: cin, cout
  Subtractor #(.width(16)) subtractor_2 (.a(a), .b(b), .out(outSub));  // open: bin, bout
  Multiplier #(.width(16)) multiplier_1 (.a(a), .b(b), .out(outMult));  // open: cin, cout
  Divider #(.width(16)) divider_1 (.a(a), .b(b), .out(outDiv));  // open: upper, rem
  Shifter #(.width(16)) shifter_1 (.in(a), .\dist (b[3:0]), .out(outLeftShift));
  assign outAnd = a & b;  // AND_Gate and_1, 16 bits wide
  assign outOr = a | b;  // OR_Gate or_1, 16 bits wide
  assign outXor = a ^ b;  // XOR_Gate xor_1, 16 bits wide
  assign outNand = ~(a & b);  // NAND_Gate nand_1, 16 bits wide
  Shifter #(.width(16), .shift("lr")) shifter_2 (.in(a), .\dist (b[3:0]), .out(outRightShift));
  Comparator #(.width(16)) comparator_1 (.a(a), .b(b), .gt(outGreater), .eq(isEqual), .lt(outLess));
endmodule

module SetReset_SR (
  input  Set,
  input  Reset,
  output Memory
);

  wire and_1_out, and_2_out, not_1_out, not_3_out;

  not not_1 (not_1_out, Set);
  not not_2 (Memory, and_1_out);
  and and_1 (and_1_out, not_1_out, not_3_out);
  and and_2 (and_2_out, Memory, Reset);
  not not_3 (not_3_out, and_2_out);
endmodule

module LatchD__noClock (
  input  Data,
  input  Enable,
  output out_3
);

  wire and_1_out, and_2_out, and_3_out, and_4_out, not_1_out, not_2_out, not_3_out, not_5_out, undriven;

  not not_1 (not_1_out, Data);
  and and_1 (and_1_out, Data, undriven);
  not not_2 (not_2_out, and_1_out);
  and and_2 (and_2_out, not_2_out, not_5_out);
  not not_3 (not_3_out, and_3_out);
  and and_3 (and_3_out, undriven, not_1_out);
  not not_4 (out_3, and_2_out);
  and and_4 (and_4_out, out_3, not_3_out);
  not not_5 (not_5_out, and_4_out);

  assign Enable = Data;
endmodule

module Reg (
  input  Clock,
  input  Enable,
  input  Reset,
  input  [3:0] AddressA,
  input  [3:0] AddressB,
  input  [15:0] Data,
  output [15:0] SaidaA,
  output [15:0] SaidaB
);

  wire dmxEnable1, dmxEnable2, dmxEnable3, dmxEnable4, dmxEnable5, dmxEnable6, dmxEnable7, dmxEnable8,
       dmxEnable9, dmxEnable10, dmxEnable11, dmxEnable12, dmxEnable13, dmxEnable14, dmxEnable15, dmxEnable16;
  wire [15:0] Reg1, Reg2, Reg3, Reg4, Reg5, Reg6, Reg7, Reg8, Reg9, Reg10, Reg11, Reg12, Reg13, Reg14, Reg15,
       Reg16;

  Register #(.width(16)) register_1 (.D(Data), .en(dmxEnable1), .Q(Reg1), .clk(Clock), .clr(Reset));
  Register #(.width(16)) register_2 (.D(Data), .en(dmxEnable2), .Q(Reg2), .clk(Clock), .clr(Reset));
  Register #(.width(16)) register_3 (.D(Data), .en(dmxEnable5), .Q(Reg5), .clk(Clock), .clr(Reset));
  Register #(.width(16)) register_4 (.D(Data), .en(dmxEnable7), .Q(Reg7), .clk(Clock), .clr(Reset));
  Register #(.width(16)) register_5 (.D(Data), .en(dmxEnable3), .Q(Reg3), .clk(Clock), .clr(Reset));
  Register #(.width(16)) register_6 (.D(Data), .en(dmxEnable4), .Q(Reg4), .clk(Clock), .clr(Reset));
  Register #(.width(16)) register_7 (.D(Data), .en(dmxEnable6), .Q(Reg6), .clk(Clock), .clr(Reset));
  Register #(.width(16)) register_8 (.D(Data), .en(dmxEnable8), .Q(Reg8), .clk(Clock), .clr(Reset));
  Demultiplexer #(.select(4)) demultiplexer_1 (
    .out0(dmxEnable1), .out1(dmxEnable2), .out2(dmxEnable3), .out3(dmxEnable4), .out4(dmxEnable5),
    .out5(dmxEnable6), .out6(dmxEnable7), .out7(dmxEnable8), .out8(dmxEnable9), .out9(dmxEnable10),
    .out10(dmxEnable11), .out11(dmxEnable12), .out12(dmxEnable13), .out13(dmxEnable14), .out14(dmxEnable15),
    .out15(dmxEnable16), .in(Enable), .sel(AddressA));  // open: en
  Register #(.width(16)) register_9 (.D(Data), .en(dmxEnable9), .Q(Reg9), .clk(Clock), .clr(Reset));
  Register #(.width(16)) register_10 (.D(Data), .en(dmxEnable11), .Q(Reg11), .clk(Clock), .clr(Reset));
  Register #(.width(16)) register_11 (.D(Data), .en(dmxEnable13), .Q(Reg13), .clk(Clock), .clr(Reset));
  Register #(.width(16)) register_12 (.D(Data), .en(dmxEnable15), .Q(Reg15), .clk(Clock), .clr(Reset));
  Register #(.width(16)) register_13 (.D(Data), .en(dmxEnable10), .Q(Reg10), .clk(Clock), .clr(Reset));
  Register #(.width(16)) register_14 (.D(Data), .en(dmxEnable12), .Q(Reg12), .clk(Clock), .clr(Reset));
  Register #(.width(16)) register_15 (.D(Data), .en(dmxEnable14), .Q(Reg14), .clk(Clock), .clr(Reset));
  Register #(.width(16)) register_16 (.D(Data), .en(dmxEnable16), .Q(Reg16), .clk(Clock), .clr(Reset));
  Multiplexer #(.select(4), .width(16)) multiplexer_1 (
    .in0(Reg1), .in1(Reg2), .in2(Reg3), .in3(Reg4), .in4(Reg5), .in5(Reg6), .in6(Reg7), .in7(Reg8),
    .in8(Reg9), .in9(Reg10), .in10(Reg11), .in11(Reg12), .in12(Reg13), .in13(Reg14), .in14(Reg15),
    .in15(Reg16), .out(SaidaA), .sel(AddressA));  // open: en
  Multiplexer #(.select(4), .width(16)) multiplexer_2 (
    .in0(Reg1), .in1(Reg2), .in2(Reg3), .in3(Reg4), .in4(Reg5), .in5(Reg6), .in6(Reg7), .in7(Reg8),
    .in8(Reg9), .in9(Reg10), .in10(Reg11), .in11(Reg12), .in12(Reg13), .in13(Reg14), .in14(Reg15),
    .in15(Reg16), .out(SaidaB), .sel(AddressB));  // open: en
endmodule

module LatchD (
  input  Data,
  input  Clock,
  output out_3
);

  wire and_2_out, and_3_out, not_1_out, not_2_out, not_3_out, undriven;

  and and_1 (Data, 1'b1, Clock);
  not not_1 (not_1_out, Data);
  not not_2 (not_2_out, and_2_out);
  and and_2 (and_2_out, Data, undriven);
  and and_3 (and_3_out, undriven, not_1_out);
  not not_3 (not_3_out, and_3_out);
  SetReset_SR setreset_sr_1 (.Set(not_2_out), .Reset(not_3_out), .Memory(out_3));
endmodule

module FlipFlop (
  input  Data,
  input  Enable,
  input  Clock,
  output Memory
);

  wire and_1_out, and_2_out, and_3_out, and_4_out, and_5_out, and_6_out, and_7_out, and_8_out, and_9_out,
       not_1_out, not_2_out, not_3_out, not_4_out, not_5_out, not_6_out, not_7_out, not_8_out, not_9_out,
       not_11_out;

  and and_1 (and_1_out, Enable, Clock);
  not not_1 (not_1_out, Data);
  not not_2 (not_2_out, Clock);
  not not_3 (not_3_out, and_2_out);
  and and_2 (and_2_out, Data, and_1_out);
  and and_3 (and_3_out, not_3_out, not_6_out);
  not not_4 (not_4_out, and_4_out);
  and and_4 (and_4_out, and_1_out, not_1_out);
  not not_5 (not_5_out, and_3_out);
  not not_6 (not_6_out, and_5_out);
  and and_5 (and_5_out, not_5_out, not_4_out);
  and and_6 (and_6_out, not_5_out, not_2_out);
  and and_7 (and_7_out, not_2_out, not_7_out);
  not not_7 (not_7_out, not_5_out);
  not not_8 (not_8_out, and_6_out);
  and and_8 (and_8_out, not_8_out, not_11_out);
  and and_9 (and_9_out, Memory, not_9_out);
  not not_9 (not_9_out, and_7_out);
  not not_10 (Memory, and_8_out);
  not not_11 (not_11_out, and_9_out);
endmodule
